// Logisim project RNG.circ as structural Verilog: 1 circuit, main circuit main
module main (
  input  RESET,
  input  [3:0] DATA,
  output [3:0] out_3,
  output [3:0] out_4,
  output out_5,
  output out_6,
  output [3:0] out_7,
  output out_8
);

  wire clock_1_out, clock_2_out, clock_3_out, nand_1_out, not_1_out, S1, S2, s_r_ff_1_q, ZAPIS_out;

  Button \RESET_zewnętrzny  (.out(S2));
  Clock clock_1 (.out(clock_1_out));
  Clock clock_2 (.out(clock_2_out));
  S_R_Flip_Flop s_r_ff_1 (.S(S1), .clk(clock_1_out), .R(S2), .Q(s_r_ff_1_q));  // open: Qn, preset, reset, en
  Counter #(.width(4), .max('h1), .trigger("falling")) counter_1 (
    .load(1'b1), .Q(out_3), .carry(S1), .clk(nand_1_out));  // open: D, count, clr
  nand nand_1 (nand_1_out, clock_2_out, ~s_r_ff_1_q);  // NAND_Gate
  Random #(.width(4)) random_1 (.clk(nand_1_out), .out(out_7));  // open: next, clr
  komparator_4bit_sklejka_main main_1 (.A(out_7), .A_B(out_5), .A_B_2(out_6), .A_B_3(out_8));  // open: B
  Clock ZAPIS (.out(ZAPIS_out));
  Clock clock_3 (.out(clock_3_out));
  not not_1 (not_1_out, ZAPIS_out);
  RAM #(.addrWidth(4), .dataWidth(4), .bus("separate")) ram_1 (
    .addr(out_7), .din(DATA), .data(out_4), .str(ZAPIS_out), .sel(1'b1), .clk(clock_3_out), .ld(not_1_out),
    .clr(S2));

  // Notes on the sheet:
  //   Tutaj ustaw 1 przed włączeniem
endmodule
