// Logisim project SAPER.circ as structural Verilog: 1 circuit, main circuit main
module main (
  input  [3:0] in_1,
  input  [3:0] in_2,
  input  [3:0] in_3,
  input  [3:0] in_4,
  input  [3:0] in_5,
  input  [3:0] in_6,
  input  [3:0] in_7,
  input  [3:0] in_8,
  input  [3:0] in_9,
  input  [3:0] in_10,
  input  [3:0] in_11,
  input  [3:0] in_12,
  input  [3:0] in_13,
  input  [3:0] in_14,
  input  [3:0] in_15,
  input  [3:0] in_16,
  input  [3:0] in_17,
  input  [3:0] in_18,
  input  [3:0] in_19,
  input  [3:0] in_20,
  input  [3:0] in_21,
  output [3:0] out_22,
  output koniec_gry,
  output [4:0] out_24,
  output [4:0] out_25
);

  wire and_1_out, clock_1_out, main_2_out_8, START_2_out, START_out,
       sterowanie_z_klawiatury_1_przemiesc_kursor;
  wire [1:0] main_1_out_2;
  wire [2:0] sterowanie_z_klawiatury_1__3_a_4_s_1_d_6_w_5_enter,
       uklad_zmiany_sterowania_z_3bit_na_5bit_1_out_x__3bit,
       uklad_zmiany_sterowania_z_3bit_na_5bit_1_out_xy_3bit;
  wire [3:0] main_3_out_3, main_4_out_3, main_5_out_3, main_6_out_3,
       uklad_przesylu_wartosci_do_wyswietlania_1_o_00, uklad_przesylu_wartosci_do_wyswietlania_1_o_01,
       uklad_przesylu_wartosci_do_wyswietlania_1_o_02, uklad_przesylu_wartosci_do_wyswietlania_1_o_03;
  wire [5:0] main_1_out_3;
  wire [6:0] keyboard_1_data;
  wire [24:0] controlled_buffer_2_out, main_7_we, pull_resistor_2_node, rom_1_data;
  wire [30:0] main_7_out_30, main_7_out_31, main_7_out_32, main_7_out_33, main_7_out_34, main_7_out_35,
       main_7_out_36, main_7_out_37, main_7_out_38, main_7_out_39, main_7_out_40, main_7_out_41,
       main_7_out_42, main_7_out_43, main_7_out_44, main_7_out_45, main_7_out_46, main_7_out_47,
       main_7_out_48, main_7_out_49, main_7_out_50, main_7_out_51, main_7_out_52, main_7_out_53,
       main_7_out_54, main_7_out_55, main_7_out_56, main_7_out_57, main_7_out_58, main_7_out_59,
       main_7_out_60;

  Maszyna_Los_XY22_main main_1 (.START(START_2_out), .out_3(main_1_out_3), .out_2(main_1_out_2));
  \porównywacz_main  main_2 (
    .in_1(main_1_out_2), .in_2(main_1_out_3), .in_3(START_2_out), .in_6(and_1_out), .out_7(out_22),
    .in_4(out_25), .in_5(out_24), .out_8(main_2_out_8));
  Pull_Resistor pull_resistor_1 (.node(main_2_out_8));
  Sterowanie_z_klawiatury sterowanie_z_klawiatury_1 (
    .\input (keyboard_1_data), ._3_a_4_s_1_d_6_w_5_enter(sterowanie_z_klawiatury_1__3_a_4_s_1_d_6_w_5_enter),
    .przemiesc_kursor(sterowanie_z_klawiatury_1_przemiesc_kursor));
  S_R_Flip_Flop #(.trigger("high")) s_r_ff_1 (
    .S(main_2_out_8), .clk(1'b1), .R(1'b0), .Q(koniec_gry));  // open: Qn, preset, reset, en
  and and_1 (and_1_out, sterowanie_z_klawiatury_1__3_a_4_s_1_d_6_w_5_enter[0], sterowanie_z_klawiatury_1__3_a_4_s_1_d_6_w_5_enter[2]);
  Clock clock_1 (.out(clock_1_out));
  Keyboard #(.buflen(1)) keyboard_1 (.clk(clock_1_out), .data(keyboard_1_data));  // open: re, clr, avail
  uklad_zwracajacy_pozycje uklad_zwracajacy_pozycje_1 (
    .Sterowanie(sterowanie_z_klawiatury_1__3_a_4_s_1_d_6_w_5_enter),
    .Move(sterowanie_z_klawiatury_1_przemiesc_kursor), .Poz_X(out_24), .Poz_Y(out_25));
  Uklad_zmiany_sterowania_z_3bit_na_5bit uklad_zmiany_sterowania_z_3bit_na_5bit_1 (
    .IN_X_5bit(out_24), .IN_Y_5bit(out_25),
    .OUT_X__3bit(uklad_zmiany_sterowania_z_3bit_na_5bit_1_out_x__3bit),
    .OUT_XY_3bit(uklad_zmiany_sterowania_z_3bit_na_5bit_1_out_xy_3bit));
  Uklad_przesylu_wartosci_do_wyswietlania uklad_przesylu_wartosci_do_wyswietlania_1 (
    .IN_Value(out_22), .IN_X(uklad_zmiany_sterowania_z_3bit_na_5bit_1_out_x__3bit),
    .IN_Y(uklad_zmiany_sterowania_z_3bit_na_5bit_1_out_xy_3bit),
    .O_00(uklad_przesylu_wartosci_do_wyswietlania_1_o_00),
    .O_01(uklad_przesylu_wartosci_do_wyswietlania_1_o_01),
    .O_02(uklad_przesylu_wartosci_do_wyswietlania_1_o_02),
    .O_03(uklad_przesylu_wartosci_do_wyswietlania_1_o_03));  // open: O_04, O_05, O_06, O_07, O_08, O_09, O_10, O_11, O_12, O_13, O_14, O_15, O_16, O_17, O_18, O_19, O_20, O_21, O_22, O_23, O_24
  Button START (.out(START_out));
  Button START_2 (.out(START_2_out));
  ROM #(.addrWidth(10), .dataWidth(25)) rom_1 (.addr({out_25, out_24}), .data(rom_1_data));  // open: sel
  przezutnik_4_bitkowy_main main_3 (
    .in_1(START_out), .in_2(uklad_przesylu_wartosci_do_wyswietlania_1_o_00), .out_3(main_3_out_3));
  przezutnik_4_bitkowy_main main_4 (
    .in_1(START_out), .in_2(uklad_przesylu_wartosci_do_wyswietlania_1_o_01), .out_3(main_4_out_3));
  przezutnik_4_bitkowy_main main_5 (
    .in_1(START_out), .in_2(uklad_przesylu_wartosci_do_wyswietlania_1_o_02), .out_3(main_5_out_3));
  przezutnik_4_bitkowy_main main_6 (
    .in_1(START_out), .in_2(uklad_przesylu_wartosci_do_wyswietlania_1_o_03), .out_3(main_6_out_3));
  ukadtest4_main main_7 (
    .in_1(main_3_out_3), .in_2(main_4_out_3), .in_3(main_5_out_3), .in_4(main_6_out_3), .in_5(in_1),
    .in_6(in_2), .in_7(in_3), .in_8(in_4), .in_9(in_5), .in_10(in_6), .in_11(in_7), .in_12(in_8),
    .in_13(in_9), .in_14(in_10), .in_15(in_11), .in_16(in_12), .in_17(in_13), .in_18(in_14), .in_19(in_15),
    .in_20(in_16), .in_21(in_17), .in_22(in_18), .in_23(in_19), .in_24(in_20), .in_25(in_21),
    .\pamięć (rom_1_data), .we(main_7_we), .wy(pull_resistor_2_node), .przycisk(START_2_out),
    .out_30(main_7_out_30), .out_31(main_7_out_31), .out_32(main_7_out_32), .out_33(main_7_out_33),
    .out_34(main_7_out_34), .out_35(main_7_out_35), .out_36(main_7_out_36), .out_37(main_7_out_37),
    .out_38(main_7_out_38), .out_39(main_7_out_39), .out_40(main_7_out_40), .out_41(main_7_out_41),
    .out_42(main_7_out_42), .out_43(main_7_out_43), .out_44(main_7_out_44), .out_45(main_7_out_45),
    .out_46(main_7_out_46), .out_47(main_7_out_47), .out_48(main_7_out_48), .out_49(main_7_out_49),
    .out_50(main_7_out_50), .out_51(main_7_out_51), .out_52(main_7_out_52), .out_53(main_7_out_53),
    .out_54(main_7_out_54), .out_55(main_7_out_55), .out_56(main_7_out_56), .out_57(main_7_out_57),
    .out_58(main_7_out_58), .out_59(main_7_out_59), .out_60(main_7_out_60));  // open: RESET
  Pull_Resistor pull_resistor_2 (.node(pull_resistor_2_node));
  assign pull_resistor_2_node = and_1_out ? controlled_buffer_2_out : 25'bz;  // Controlled_Buffer controlled_buffer_1
  assign controlled_buffer_2_out = and_1_out ? main_7_we : 25'bz;  // Controlled_Buffer controlled_buffer_2
  DotMatrix #(.inputtype("row"), .matrixcols(31), .matrixrows(31)) dotmatrix_1 (
    .row0(main_7_out_30), .row1(main_7_out_31), .row2(main_7_out_32), .row3(main_7_out_33),
    .row4(main_7_out_34), .row5(main_7_out_35), .row6(main_7_out_36), .row7(main_7_out_37),
    .row8(main_7_out_38), .row9(main_7_out_39), .row10(main_7_out_40), .row11(main_7_out_41),
    .row12(main_7_out_42), .row13(main_7_out_43), .row14(main_7_out_44), .row15(main_7_out_45),
    .row16(main_7_out_46), .row17(main_7_out_47), .row18(main_7_out_48), .row19(main_7_out_49),
    .row20(main_7_out_50), .row21(main_7_out_51), .row22(main_7_out_52), .row23(main_7_out_53),
    .row24(main_7_out_54), .row25(main_7_out_55), .row26(main_7_out_56), .row27(main_7_out_57),
    .row28(main_7_out_58), .row29(main_7_out_59), .row30(main_7_out_60));

  // Other names for the same wires on the sheet: X1[4:0] = out_24; Y1[4:0] = out_25

  // Notes on the sheet:
  //   contents of rom_1 (hex, n*v repeats v):
  //   33*0 1efffff 1dfffff 0 1bfffff 0 0 0 17fffff 7*0 ffffff 16*0 1ff7fff 1feffff 0 1fdffff 0 0 0 1fbffff
  //   7*0 1f7ffff 48*0 1fffbff 1fff7ff 0 1ffefff 0 0 0 1ffdfff 7*0 1ffbfff 111*0 1fffdff 1ffffdf 1ffffbf 0
  //   1ffff7f 0 0 0 1fffeff 7*0 1fffdff 1ffffdf 1ffffbf 0 1ffff7f 236*0 1fffffe 1fffffd 0 1fffffb 0 0 0
  //   1fffff7 7*0 1ffffef
endmodule
