// Logisim project 4bityx.circ as structural Verilog: 1 circuit, main circuit main
module main (
  input  ENTER,
  input  [3:0] \WEJŚCIE ,
  input  RESET,
  output [3:0] \WYJŚCIE 
);

  wire and_1_out, d_ff_1_q, or_1_out, or_2_out, or_3_out;

  and and_1 (and_1_out, ENTER, or_1_out);
  D_Flip_Flop #(.trigger("falling")) d_ff_1 (
    .clk(and_1_out), .D(1'b1), .Q(d_ff_1_q), .reset(RESET));  // open: Qn, preset, en
  D_Flip_Flop d_ff_2 (.clk(d_ff_1_q), .D(\WEJŚCIE [0]), .Q(\WYJŚCIE [0]), .reset(RESET));  // open: Qn, preset, en
  D_Flip_Flop d_ff_3 (.clk(d_ff_1_q), .D(\WEJŚCIE [1]), .Q(\WYJŚCIE [1]), .reset(RESET));  // open: Qn, preset, en
  or or_1 (or_1_out, or_2_out, or_3_out);
  or or_2 (or_2_out, \WEJŚCIE [0], \WEJŚCIE [1]);
  or or_3 (or_3_out, \WEJŚCIE [2], \WEJŚCIE [3]);
  D_Flip_Flop d_ff_4 (.clk(d_ff_1_q), .D(\WEJŚCIE [2]), .Q(\WYJŚCIE [2]), .reset(RESET));  // open: Qn, preset, en
  D_Flip_Flop d_ff_5 (.clk(d_ff_1_q), .D(\WEJŚCIE [3]), .Q(\WYJŚCIE [3]), .reset(RESET));  // open: Qn, preset, en
endmodule
