// Logisim project SAPER.circ as structural Verilog: 1 circuit, main circuit main
module main (
  output [3:0] out_1,
  output [3:0] out_2,
  output [5:0] out_3,
  output koniec_gry
);

  wire clock_1_out, E1, M1, main_2_p3, main_2_p8;
  wire [1:0] main_1_out_2;
  wire [2:0] uklad_zmiany_sterowania_z_3bit_na_5bit_1_out_x__3bit,
       uklad_zmiany_sterowania_z_3bit_na_5bit_1_out_xy_3bit;
  wire [4:0] X1, Y1;
  wire [5:0] main_1_out_3;
  wire [6:0] keyboard_1_data;
  wire [24:0] \sterowanie_dużo_1_nr_zaznaczonego_pola ;
  wire [30:0] main_3_out_7, main_3_out_8, main_3_out_9, main_3_out_10, main_3_out_11, main_3_out_12,
       main_3_out_13, main_3_out_14, main_3_out_15, main_3_out_16, main_3_out_17, main_3_out_18,
       main_3_out_19, main_3_out_20, main_3_out_21, main_3_out_22, main_3_out_23, main_3_out_24,
       main_3_out_25, main_3_out_26, main_3_out_27, main_3_out_28, main_3_out_29, main_3_out_30,
       main_3_out_31, main_3_out_32, main_3_out_33, main_3_out_34, main_3_out_35, main_3_out_36,
       main_3_out_37;

  Maszyna_Los_XY22_main main_1 (.START(main_2_p3), .out_3(main_1_out_3), .out_2(main_1_out_2));
  Clock #(.highDuration(4), .lowDuration(4)) clock_1 (.out(clock_1_out));
  Uklad_zmiany_sterowania_z_3bit_na_5bit uklad_zmiany_sterowania_z_3bit_na_5bit_1 (
    .IN_X_5bit(X1), .IN_Y_5bit(Y1), .OUT_X__3bit(uklad_zmiany_sterowania_z_3bit_na_5bit_1_out_x__3bit),
    .OUT_XY_3bit(uklad_zmiany_sterowania_z_3bit_na_5bit_1_out_xy_3bit));
  Keyboard #(.buflen(1)) keyboard_1 (.clk(clock_1_out), .data(keyboard_1_data));  // open: re, clr, avail
  // porównywacz_main main_2: pin names not known; wires that end beside it: main_1_out_2, main_1_out_3, main_2_p3, uklad_zmiany_sterowania_z_3bit_na_5bit_1_out_x__3bit, E1, uklad_zmiany_sterowania_z_3bit_na_5bit_1_out_xy_3bit, Y1, main_2_p8, X1, out_2, out_3
  Pull_Resistor pull_resistor_1 (.node(main_2_p8));
  S_R_Flip_Flop #(.trigger("high")) s_r_ff_1 (
    .S(main_2_p8), .clk(1'b1), .R(main_2_p3), .Q(koniec_gry));  // open: Qn, preset, reset, en
  \Sterowanie_dużo  \sterowanie_dużo_1  (
    .Wejscie_Klawiatury(keyboard_1_data), .Nr_Zaznaczonego_pola(\sterowanie_dużo_1_nr_zaznaczonego_pola ),
    .Enter(E1), .M(M1), .X(X1), .Y(Y1));
  Register #(.width(4)) register_1 (.D(out_2), .Q(out_1), .clk(E1));  // open: en, clr
  Button START (.out(main_2_p3));
  SAPER2_main main_3 (
    .x(X1), .Y(Y1), .WYJSCIE(out_2), .START(main_2_p3), .PAMIEC(\sterowanie_dużo_1_nr_zaznaczonego_pola ),
    .ENTER(E1), .out_7(main_3_out_7), .out_8(main_3_out_8), .out_9(main_3_out_9), .out_10(main_3_out_10),
    .out_11(main_3_out_11), .out_12(main_3_out_12), .out_13(main_3_out_13), .out_14(main_3_out_14),
    .out_15(main_3_out_15), .out_16(main_3_out_16), .out_17(main_3_out_17), .out_18(main_3_out_18),
    .out_19(main_3_out_19), .out_20(main_3_out_20), .out_21(main_3_out_21), .out_22(main_3_out_22),
    .out_23(main_3_out_23), .out_24(main_3_out_24), .out_25(main_3_out_25), .out_26(main_3_out_26),
    .out_27(main_3_out_27), .out_28(main_3_out_28), .out_29(main_3_out_29), .out_30(main_3_out_30),
    .out_31(main_3_out_31), .out_32(main_3_out_32), .out_33(main_3_out_33), .out_34(main_3_out_34),
    .out_35(main_3_out_35), .out_36(main_3_out_36), .out_37(main_3_out_37));
  DotMatrix #(.inputtype("row"), .matrixcols(31), .matrixrows(31)) dotmatrix_1 (
    .row0(main_3_out_7), .row1(main_3_out_8), .row2(main_3_out_9), .row3(main_3_out_10),
    .row4(main_3_out_11), .row5(main_3_out_12), .row6(main_3_out_13), .row7(main_3_out_14),
    .row8(main_3_out_15), .row9(main_3_out_16), .row10(main_3_out_17), .row11(main_3_out_18),
    .row12(main_3_out_19), .row13(main_3_out_20), .row14(main_3_out_21), .row15(main_3_out_22),
    .row16(main_3_out_23), .row17(main_3_out_24), .row18(main_3_out_25), .row19(main_3_out_26),
    .row20(main_3_out_27), .row21(main_3_out_28), .row22(main_3_out_29), .row23(main_3_out_30),
    .row24(main_3_out_31), .row25(main_3_out_32), .row26(main_3_out_33), .row27(main_3_out_34),
    .row28(main_3_out_35), .row29(main_3_out_36), .row30(main_3_out_37));

  // Notes on the sheet:
  //   ogólnie restartownie układu poprzez przycisk start na razie nie działa 
endmodule
