// Logisim project BOOMBOX.circ as structural Verilog: 1 circuit, main circuit main
module main (
  input  [1:0] in_1,
  input  [5:0] in_2,
  input  in_3,
  input  in_4,
  input  [5:0] in_5,
  input  in_6,
  output out_7
);

  wire and_3_out, clock_1_out, clock_2_out, clock_3_out, clock_4_out, clock_5_out, clock_6_out, clock_7_out,
       comparator_1_eq, controlled_buffer_1_out, controlled_buffer_2_out, not_1_out, not_2_out, not_3_out,
       S1, S2, S4, s_r_ff_4_q, Z1, Z4, Z5;
  wire [1:0] and_2_out, counter_3_q, or_2_out;
  wire [1:1] K1;
  wire [5:0] controlled_buffer_3_out, ram_1_data;

  Clock clock_1 (.out(clock_1_out));
  Clock clock_2 (.out(clock_2_out));
  Clock clock_3 (.out(clock_3_out));
  Clock clock_4 (.out(clock_4_out));
  or or_1 (S2, in_3, in_3);
  not not_1 (not_1_out, S2);
  assign controlled_buffer_1_out = not_1_out ? clock_1_out : 1'bz;  // Controlled_Buffer controlled_buffer_1
  S_R_Flip_Flop s_r_ff_1 (.S(S1), .clk(clock_2_out), .R(S2), .Q(K1[1]));  // open: Qn, preset, reset, en
  not not_2 (not_2_out, in_4);
  assign controlled_buffer_2_out = not_2_out ? clock_3_out : 1'bz;  // Controlled_Buffer controlled_buffer_2
  S_R_Flip_Flop s_r_ff_2 (.S(Z1), .clk(clock_4_out), .R(in_4), .Q(Z5));  // open: Qn, preset, reset, en
  Pull_Resistor pull_resistor_1 (.node(controlled_buffer_1_out));
  nand nand_1 (S4, controlled_buffer_1_out, ~K1[1]);  // NAND_Gate
  Pull_Resistor pull_resistor_2 (.node(controlled_buffer_2_out));
  and and_1 (Z4, controlled_buffer_2_out, ~Z5);  // AND_Gate
  Counter #(.width(4), .max('h8), .trigger("falling")) counter_1 (
    .load(1'b1), .carry(S1), .clk(S4));  // open: D, count, Q, clr
  Counter #(.width(4), .max('h4), .trigger("falling")) counter_2 (
    .load(1'b1), .carry(Z1), .clk(Z4));  // open: D, count, Q, clr
  assign and_2_out = in_1 & ~{2{K1[1]}};  // AND_Gate and_2, 2 bits wide
  assign or_2_out = and_2_out | counter_3_q;  // OR_Gate or_2, 2 bits wide
  and and_3 (and_3_out, ~K1[1], S4);  // AND_Gate
  Comparator #(.width(6)) comparator_1 (.a(in_5), .b(controlled_buffer_3_out), .eq(comparator_1_eq));  // open: gt, lt
  Pull_Resistor pull_resistor_3 (.node(comparator_1_eq));
  Clock clock_5 (.out(clock_5_out));
  Counter #(.width(2), .max('h2), .ongoal("continue"), .trigger("falling")) counter_3 (
    .Q(counter_3_q), .clk(Z4), .clr(Z5));  // open: load, D, count, carry
  Clock clock_6 (.out(clock_6_out));
  not not_3 (not_3_out, and_3_out);
  S_R_Flip_Flop s_r_ff_3 (.S(comparator_1_eq), .clk(clock_5_out), .R(in_6), .Q(out_7));  // open: Qn, preset, reset, en
  RAM #(.addrWidth(2), .dataWidth(6), .bus("separate")) ram_1 (
    .addr(or_2_out), .din(in_2), .data(ram_1_data), .str(and_3_out), .sel(1'b1), .clk(clock_6_out), .clr(S2));  // open: ld
  Clock clock_7 (.out(clock_7_out));
  assign controlled_buffer_3_out = s_r_ff_4_q ? ram_1_data : 6'bz;  // Controlled_Buffer controlled_buffer_3
  S_R_Flip_Flop s_r_ff_4 (.S(in_4), .clk(clock_7_out), .R(Z1), .Q(s_r_ff_4_q));  // open: Qn, preset, reset, en

  // Other names for the same wires on the sheet: K1[0] = K1[1]; S5 = K1[1]; Z2 = in_4
endmodule
