// Logisim project licznik czasu.circ as structural Verilog: 5 circuits, main circuit main
module main (
  input  CLK,
  input  Stop,
  input  Start,
  output [11:0] Czas,
  output [1:0] out_5
);

  wire d_ff_1_qn, d_ff_2_qn, d_ff_3_qn, d_ff_4_qn, d_ff_5_qn, d_ff_6_qn, d_ff_7_qn, d_ff_8_qn, d_ff_9_qn,
       d_ff_10_qn, d_ff_11_qn, d_ff_12_qn, not_1_out, Stop_t;

  not not_1 (not_1_out, Stop_t);
  assign out_5[0] = not_1_out ? CLK : 1'bz;  // Controlled_Buffer controlled_buffer_1
  S_R_Flip_Flop #(.trigger("high")) s_r_ff_1 (
    .S(Stop), .clk(1'b1), .R(Start), .Q(Stop_t));  // open: Qn, preset, reset, en
  D_Flip_Flop d_ff_1 (.clk(out_5[0]), .D(d_ff_1_qn), .Q(Czas[0]), .Qn(d_ff_1_qn), .reset(Start));  // open: preset, en
  D_Flip_Flop d_ff_2 (.clk(d_ff_10_qn), .D(d_ff_2_qn), .Q(Czas[4]), .Qn(d_ff_2_qn), .reset(Start));  // open: preset, en
  D_Flip_Flop d_ff_3 (.clk(d_ff_11_qn), .D(d_ff_3_qn), .Q(Czas[8]), .Qn(d_ff_3_qn), .reset(Start));  // open: preset, en
  D_Flip_Flop d_ff_4 (.clk(d_ff_1_qn), .D(d_ff_4_qn), .Q(Czas[1]), .Qn(d_ff_4_qn), .reset(Start));  // open: preset, en
  D_Flip_Flop d_ff_5 (.clk(d_ff_2_qn), .D(d_ff_5_qn), .Q(Czas[5]), .Qn(d_ff_5_qn), .reset(Start));  // open: preset, en
  D_Flip_Flop d_ff_6 (.clk(d_ff_3_qn), .D(d_ff_6_qn), .Q(Czas[9]), .Qn(d_ff_6_qn), .reset(Start));  // open: preset, en
  D_Flip_Flop d_ff_7 (.clk(d_ff_4_qn), .D(d_ff_7_qn), .Q(Czas[2]), .Qn(d_ff_7_qn), .reset(Start));  // open: preset, en
  D_Flip_Flop d_ff_8 (.clk(d_ff_5_qn), .D(d_ff_8_qn), .Q(Czas[6]), .Qn(d_ff_8_qn), .reset(Start));  // open: preset, en
  D_Flip_Flop d_ff_9 (.clk(d_ff_6_qn), .D(d_ff_9_qn), .Q(Czas[10]), .Qn(d_ff_9_qn), .reset(Start));  // open: preset, en
  D_Flip_Flop d_ff_10 (
    .clk(d_ff_7_qn), .D(d_ff_10_qn), .Q(Czas[3]), .Qn(d_ff_10_qn), .reset(Start));  // open: preset, en
  D_Flip_Flop d_ff_11 (
    .clk(d_ff_8_qn), .D(d_ff_11_qn), .Q(Czas[7]), .Qn(d_ff_11_qn), .reset(Start));  // open: preset, en
  D_Flip_Flop d_ff_12 (
    .clk(d_ff_9_qn), .D(d_ff_12_qn), .Q(Czas[11]), .Qn(d_ff_12_qn), .reset(Start));  // open: preset, en

  assign out_5[1] = Start;

  // Other names for the same wires on the sheet: CLK_t = out_5[0]
endmodule

module wyswietlacz_czasu (
  input  [1:0] DISP_IN__1bit_reset_0bit_clk,
  output [4:0] o10,
  output [4:0] o20,
  output [4:0] o15,
  output [4:0] o9,
  output [4:0] o4,
  output [4:0] o19,
  output [4:0] o14,
  output [4:0] o8,
  output [4:0] o3,
  output [4:0] o18,
  output [4:0] o13,
  output [4:0] o7,
  output [4:0] o2,
  output [4:0] o17,
  output [4:0] o12,
  output [4:0] o6,
  output [4:0] o1,
  output [4:0] o16,
  output [4:0] o11,
  output [4:0] o5,
  output [4:0] o0
);

  wire and_1_out, and_2_out, and_3_out, and_4_out, controlled_buffer_1_out, controlled_buffer_3_out,
       controlled_buffer_5_out, controlled_buffer_7_out, licznik_4_bitowy_1_q0, licznik_4_bitowy_1_q1,
       licznik_4_bitowy_1_q2, licznik_4_bitowy_1_q3, licznik_4_bitowy_2_q0, licznik_4_bitowy_2_q1,
       licznik_4_bitowy_2_q2, licznik_4_bitowy_2_q3, licznik_4_bitowy_3_q0, licznik_4_bitowy_3_q1,
       licznik_4_bitowy_3_q2, licznik_4_bitowy_3_q3, licznik_4_bitowy_4_q0, licznik_4_bitowy_4_q1,
       licznik_4_bitowy_4_q2, licznik_4_bitowy_4_q3, not_1_out, not_2_out, not_3_out, not_4_out;

  and and_1 (and_1_out, licznik_4_bitowy_1_q2, licznik_4_bitowy_1_q1);
  not not_1 (not_1_out, DISP_IN__1bit_reset_0bit_clk[1]);
  Matrix_Dekoder matrix_dekoder_1 (
    .I_3(licznik_4_bitowy_1_q3), .I_2(licznik_4_bitowy_1_q2), .I_1(licznik_4_bitowy_1_q1),
    .I_O(licznik_4_bitowy_1_q0), .R(o19), .C(o18), .L(o17));
  licznik_4_bitowy licznik_4_bitowy_1 (
    .T(and_2_out), .Reset(controlled_buffer_1_out), .Q3(licznik_4_bitowy_1_q3), .Q2(licznik_4_bitowy_1_q2),
    .Q1(licznik_4_bitowy_1_q1), .Q0(licznik_4_bitowy_1_q0));
  assign controlled_buffer_1_out = DISP_IN__1bit_reset_0bit_clk[1] ? 1'b1 : 1'bz;  // Controlled_Buffer controlled_buffer_1
  assign controlled_buffer_1_out = not_1_out ? and_1_out : 1'bz;  // Controlled_Buffer controlled_buffer_2
  and and_2 (and_2_out, licznik_4_bitowy_2_q3, licznik_4_bitowy_2_q1);
  licznik_4_bitowy licznik_4_bitowy_2 (
    .T(and_3_out), .Reset(controlled_buffer_3_out), .Q3(licznik_4_bitowy_2_q3), .Q2(licznik_4_bitowy_2_q2),
    .Q1(licznik_4_bitowy_2_q1), .Q0(licznik_4_bitowy_2_q0));
  not not_2 (not_2_out, DISP_IN__1bit_reset_0bit_clk[1]);
  Matrix_Dekoder matrix_dekoder_2 (
    .I_3(licznik_4_bitowy_2_q3), .I_2(licznik_4_bitowy_2_q2), .I_1(licznik_4_bitowy_2_q1),
    .I_O(licznik_4_bitowy_2_q0), .R(o14), .C(o13), .L(o12));
  assign controlled_buffer_3_out = DISP_IN__1bit_reset_0bit_clk[1] ? 1'b1 : 1'bz;  // Controlled_Buffer controlled_buffer_3
  assign controlled_buffer_3_out = not_2_out ? and_2_out : 1'bz;  // Controlled_Buffer controlled_buffer_4
  Matrix_Dekoder matrix_dekoder_3 (
    .I_3(licznik_4_bitowy_3_q3), .I_2(licznik_4_bitowy_3_q2), .I_1(licznik_4_bitowy_3_q1),
    .I_O(licznik_4_bitowy_3_q0), .R(o8), .C(o7), .L(o6));
  and and_3 (and_3_out, licznik_4_bitowy_3_q2, licznik_4_bitowy_3_q1);
  licznik_4_bitowy licznik_4_bitowy_3 (
    .T(and_4_out), .Reset(controlled_buffer_5_out), .Q3(licznik_4_bitowy_3_q3), .Q2(licznik_4_bitowy_3_q2),
    .Q1(licznik_4_bitowy_3_q1), .Q0(licznik_4_bitowy_3_q0));
  assign controlled_buffer_5_out = DISP_IN__1bit_reset_0bit_clk[1] ? 1'b1 : 1'bz;  // Controlled_Buffer controlled_buffer_5
  assign controlled_buffer_5_out = not_3_out ? and_3_out : 1'bz;  // Controlled_Buffer controlled_buffer_6
  not not_3 (not_3_out, DISP_IN__1bit_reset_0bit_clk[1]);
  and and_4 (and_4_out, licznik_4_bitowy_4_q3, licznik_4_bitowy_4_q1);
  Matrix_Dekoder matrix_dekoder_4 (
    .I_3(licznik_4_bitowy_4_q3), .I_2(licznik_4_bitowy_4_q2), .I_1(licznik_4_bitowy_4_q1),
    .I_O(licznik_4_bitowy_4_q0), .R(o3), .C(o2), .L(o1));
  licznik_4_bitowy licznik_4_bitowy_4 (
    .T(DISP_IN__1bit_reset_0bit_clk[0]), .Reset(controlled_buffer_7_out), .Q3(licznik_4_bitowy_4_q3),
    .Q2(licznik_4_bitowy_4_q2), .Q1(licznik_4_bitowy_4_q1), .Q0(licznik_4_bitowy_4_q0));
  assign controlled_buffer_7_out = not_4_out ? and_4_out : 1'bz;  // Controlled_Buffer controlled_buffer_7
  assign controlled_buffer_7_out = DISP_IN__1bit_reset_0bit_clk[1] ? 1'b1 : 1'bz;  // Controlled_Buffer controlled_buffer_8
  not not_4 (not_4_out, DISP_IN__1bit_reset_0bit_clk[1]);

  assign o0 = {5{1'b0}};
  assign o4 = {5{1'b0}};
  assign o5 = {5{1'b0}};
  assign o9 = {5{1'b0}};
  assign o10 = 5'b01010;
  assign o11 = {5{1'b0}};
  assign o15 = {5{1'b0}};
  assign o16 = {5{1'b0}};
  assign o20 = {5{1'b0}};

  // Other names for the same wires on the sheet: CLK = DISP_IN__1bit_reset_0bit_clk[0];
  //   R = DISP_IN__1bit_reset_0bit_clk[1]
endmodule

module licznik_4_bitowy (
  input  T,
  input  Reset,
  output Q3,
  output Q2,
  output Q1,
  output Q0
);

  wire t_ff_1_qn, t_ff_2_qn, t_ff_3_qn;

  T_Flip_Flop t_ff_1 (.clk(T), .T(1'b1), .Q(Q0), .Qn(t_ff_1_qn), .reset(Reset));  // open: preset, en
  T_Flip_Flop t_ff_2 (.clk(t_ff_1_qn), .T(1'b1), .Q(Q1), .Qn(t_ff_2_qn), .reset(Reset));  // open: preset, en
  T_Flip_Flop t_ff_3 (.clk(t_ff_2_qn), .T(1'b1), .Q(Q2), .Qn(t_ff_3_qn), .reset(Reset));  // open: preset, en
  T_Flip_Flop t_ff_4 (.clk(t_ff_3_qn), .T(1'b1), .Q(Q3), .reset(Reset));  // open: Qn, preset, en
endmodule

module Wyswietlanie_wyniku (
  input  [11:0] \L__połączyć_z_L_z_licznika_czasu_main ,
  input  [1:0] in_2,
  output [4:0] o10,
  output [4:0] o20,
  output [4:0] o15,
  output [4:0] o9,
  output [4:0] o4,
  output [4:0] o19,
  output [4:0] o14,
  output [4:0] o8,
  output [4:0] o3,
  output [4:0] o18,
  output [4:0] o13,
  output [4:0] o7,
  output [4:0] o2,
  output [4:0] o17,
  output [4:0] o12,
  output [4:0] o6,
  output [4:0] o1,
  output [4:0] o16,
  output [4:0] o11,
  output [4:0] o5,
  output [4:0] o0
);

  wire and_1_out, and_2_out, and_3_out, and_4_out, controlled_buffer_1_out, controlled_buffer_3_out,
       controlled_buffer_5_out, controlled_buffer_8_out, Licz, licznik_4_bitowy_1_q0, licznik_4_bitowy_1_q1,
       licznik_4_bitowy_1_q2, licznik_4_bitowy_1_q3, licznik_4_bitowy_2_q0, licznik_4_bitowy_2_q1,
       licznik_4_bitowy_2_q2, licznik_4_bitowy_2_q3, licznik_4_bitowy_3_q0, licznik_4_bitowy_3_q1,
       licznik_4_bitowy_3_q2, licznik_4_bitowy_3_q3, licznik_4_bitowy_4_q0, licznik_4_bitowy_4_q1,
       licznik_4_bitowy_4_q2, licznik_4_bitowy_4_q3, not_1_out, not_2_out, not_3_out, not_4_out,
       pull_resistor_1_node;
  wire [11:0] counter_1_q, subtractor_1_out;

  Counter #(.width(12), .max('h3ff), .ongoal("stay")) counter_1 (
    .Q(counter_1_q), .clk(in_2[0]), .clr(in_2[1]));  // open: load, D, count, carry
  Subtractor #(.width(12)) subtractor_1 (
    .a(12'h3ff), .b(\L__połączyć_z_L_z_licznika_czasu_main ), .out(subtractor_1_out));  // open: bin, bout
  Comparator #(.width(12), .mode("unsigned")) comparator_1 (
    .a(counter_1_q), .b(subtractor_1_out), .lt(Licz));  // open: gt, eq
  and and_1 (and_1_out, licznik_4_bitowy_1_q3, licznik_4_bitowy_1_q1);
  not not_1 (not_1_out, in_2[1]);
  Matrix_Dekoder matrix_dekoder_1 (
    .I_3(licznik_4_bitowy_1_q3), .I_2(licznik_4_bitowy_1_q2), .I_1(licznik_4_bitowy_1_q1),
    .I_O(licznik_4_bitowy_1_q0), .R(o19), .C(o18), .L(o17));
  licznik_4_bitowy licznik_4_bitowy_1 (
    .T(and_2_out), .Reset(controlled_buffer_1_out), .Q3(licznik_4_bitowy_1_q3), .Q2(licznik_4_bitowy_1_q2),
    .Q1(licznik_4_bitowy_1_q1), .Q0(licznik_4_bitowy_1_q0));
  assign controlled_buffer_1_out = in_2[1] ? 1'b1 : 1'bz;  // Controlled_Buffer controlled_buffer_1
  assign controlled_buffer_1_out = not_1_out ? and_1_out : 1'bz;  // Controlled_Buffer controlled_buffer_2
  and and_2 (and_2_out, licznik_4_bitowy_2_q3, licznik_4_bitowy_2_q1);
  licznik_4_bitowy licznik_4_bitowy_2 (
    .T(and_3_out), .Reset(controlled_buffer_3_out), .Q3(licznik_4_bitowy_2_q3), .Q2(licznik_4_bitowy_2_q2),
    .Q1(licznik_4_bitowy_2_q1), .Q0(licznik_4_bitowy_2_q0));
  not not_2 (not_2_out, in_2[1]);
  Matrix_Dekoder matrix_dekoder_2 (
    .I_3(licznik_4_bitowy_2_q3), .I_2(licznik_4_bitowy_2_q2), .I_1(licznik_4_bitowy_2_q1),
    .I_O(licznik_4_bitowy_2_q0), .R(o14), .C(o13), .L(o12));
  assign controlled_buffer_3_out = in_2[1] ? 1'b1 : 1'bz;  // Controlled_Buffer controlled_buffer_3
  assign controlled_buffer_3_out = not_2_out ? and_2_out : 1'bz;  // Controlled_Buffer controlled_buffer_4
  Matrix_Dekoder matrix_dekoder_3 (
    .I_3(licznik_4_bitowy_3_q3), .I_2(licznik_4_bitowy_3_q2), .I_1(licznik_4_bitowy_3_q1),
    .I_O(licznik_4_bitowy_3_q0), .R(o8), .C(o7), .L(o6));
  and and_3 (and_3_out, licznik_4_bitowy_3_q3, licznik_4_bitowy_3_q1);
  licznik_4_bitowy licznik_4_bitowy_3 (
    .T(and_4_out), .Reset(controlled_buffer_5_out), .Q3(licznik_4_bitowy_3_q3), .Q2(licznik_4_bitowy_3_q2),
    .Q1(licznik_4_bitowy_3_q1), .Q0(licznik_4_bitowy_3_q0));
  assign controlled_buffer_5_out = in_2[1] ? 1'b1 : 1'bz;  // Controlled_Buffer controlled_buffer_5
  assign controlled_buffer_5_out = not_3_out ? and_3_out : 1'bz;  // Controlled_Buffer controlled_buffer_6
  not not_3 (not_3_out, in_2[1]);
  and and_4 (and_4_out, licznik_4_bitowy_4_q3, licznik_4_bitowy_4_q1);
  Matrix_Dekoder matrix_dekoder_4 (
    .I_3(licznik_4_bitowy_4_q3), .I_2(licznik_4_bitowy_4_q2), .I_1(licznik_4_bitowy_4_q1),
    .I_O(licznik_4_bitowy_4_q0), .R(o3), .C(o2), .L(o1));
  licznik_4_bitowy licznik_4_bitowy_4 (
    .T(pull_resistor_1_node), .Reset(controlled_buffer_8_out), .Q3(licznik_4_bitowy_4_q3),
    .Q2(licznik_4_bitowy_4_q2), .Q1(licznik_4_bitowy_4_q1), .Q0(licznik_4_bitowy_4_q0));
  Pull_Resistor pull_resistor_1 (.node(pull_resistor_1_node));
  assign pull_resistor_1_node = Licz ? in_2[0] : 1'bz;  // Controlled_Buffer controlled_buffer_7
  assign controlled_buffer_8_out = not_4_out ? and_4_out : 1'bz;  // Controlled_Buffer controlled_buffer_8
  assign controlled_buffer_8_out = in_2[1] ? 1'b1 : 1'bz;  // Controlled_Buffer controlled_buffer_9
  not not_4 (not_4_out, in_2[1]);

  assign o0 = {5{1'b0}};
  assign o4 = {5{1'b0}};
  assign o5 = {5{1'b0}};
  assign o9 = {5{1'b0}};
  assign o10 = {5{1'b0}};
  assign o11 = {5{1'b0}};
  assign o15 = {5{1'b0}};
  assign o16 = {5{1'b0}};
  assign o20 = {5{1'b0}};

  // Other names for the same wires on the sheet: CLK = in_2[0]; R = in_2[1]
endmodule

module Matrix_Dekoder (
  input  I_3,
  input  I_2,
  input  I_1,
  input  I_O,
  output [4:0] R,
  output [4:0] C,
  output [4:0] L
);

  ROM #(.addrWidth(4), .dataWidth(15)) rom_1 (.addr({I_3, I_2, I_1, I_O}), .data({R, C, L}));  // open: sel

  // Notes on the sheet:
  //   contents of rom_1 (hex, n*v repeats v):
  //   7e3f 3e0 5ebd 56bf 709f 76b7 7eb7 421f 7ebf 76bf
endmodule
