// Logisim project lose.circ as structural Verilog: 1 circuit, main circuit main
module main (
  input  [1:0] in_1,
  output [4:0] _1,
  output [4:0] out_3,
  output [4:0] out_4,
  output [4:0] out_5,
  output [4:0] out_6,
  output [4:0] out_7,
  output [4:0] out_8,
  output [4:0] out_9,
  output [4:0] out_10,
  output [4:0] out_11,
  output [4:0] out_12,
  output [4:0] out_13,
  output [4:0] out_14,
  output [4:0] out_15,
  output [4:0] out_16,
  output [4:0] out_17,
  output [4:0] out_18,
  output [4:0] out_19,
  output [4:0] out_20,
  output [4:0] out_21,
  output [4:0] out_22,
  output [4:0] out_23,
  output [4:0] out_24,
  output [4:0] out_25,
  output [4:0] out_26,
  output [4:0] out_27,
  output [4:0] out_28,
  output [4:0] out_29,
  output [4:0] out_30,
  output [4:0] out_31,
  output [4:0] l
);

  ROM #(.addrWidth(2), .dataWidth(30)) rom_1 (
    .addr(in_1), .data({out_21, out_20, out_19, out_18, out_17, out_16}));  // open: sel
  ROM #(.addrWidth(2), .dataWidth(20)) rom_2 (.addr(in_1), .data({out_25, out_24, out_23, out_22}));  // open: sel
  ROM #(.addrWidth(2), .dataWidth(30)) rom_3 (
    .addr(in_1), .data({out_15, out_14, out_13, out_12, out_11, out_10}));  // open: sel

  assign _1 = {5{1'b0}};
  assign l = {5{1'b0}};
  assign out_3 = {5{1'b0}};
  assign out_4 = {5{1'b0}};
  assign out_5 = {5{1'b0}};
  assign out_6 = {5{1'b0}};
  assign out_7 = {5{1'b0}};
  assign out_8 = {5{1'b0}};
  assign out_9 = {5{1'b0}};
  assign out_26 = {5{1'b0}};
  assign out_27 = {5{1'b0}};
  assign out_28 = {5{1'b0}};
  assign out_29 = {5{1'b0}};
  assign out_30 = {5{1'b0}};
  assign out_31 = {5{1'b0}};

  // Notes on the sheet:
  //   contents of rom_1 (hex, n*v repeats v):
  //   3f0f83e0 17af41f
  //   contents of rom_2 (hex, n*v repeats v):
  //   0 56bf
  //   contents of rom_3 (hex, n*v repeats v):
  //   3e1f87e0 23f0043f
endmodule
