// Logisim project Sterowanie.circ as structural Verilog: 6 circuits, main circuit Sterowanie z klawiatury
module Sterowanie_z_klawiatury (
  input  [6:0] \input ,
  output [2:0] _3_a_4_s_1_d_6_w_5_enter,
  output przemiesc_kursor
);

  wire [4:0] komparator_7bit_do_sterowania_1__1_oznacza_ze_jest_rowne;

  Komparator_7bit_do_sterowania komparator_7bit_do_sterowania_1 (
    .A(\input ), .B(7'b1100001),
    ._1_oznacza_ze_jest_rowne(komparator_7bit_do_sterowania_1__1_oznacza_ze_jest_rowne[0]));
  Komparator_7bit_do_sterowania komparator_7bit_do_sterowania_2 (
    .A(\input ), .B(7'b1110011),
    ._1_oznacza_ze_jest_rowne(komparator_7bit_do_sterowania_1__1_oznacza_ze_jest_rowne[1]));
  Komparator_7bit_do_sterowania komparator_7bit_do_sterowania_3 (
    .A(\input ), .B(7'b1100100),
    ._1_oznacza_ze_jest_rowne(komparator_7bit_do_sterowania_1__1_oznacza_ze_jest_rowne[2]));
  Komparator_7bit_do_sterowania komparator_7bit_do_sterowania_4 (
    .A(\input ), .B(7'b1110111),
    ._1_oznacza_ze_jest_rowne(komparator_7bit_do_sterowania_1__1_oznacza_ze_jest_rowne[3]));
  Komparator_7bit_do_sterowania komparator_7bit_do_sterowania_5 (
    .A(\input ), .B(7'b0001010),
    ._1_oznacza_ze_jest_rowne(komparator_7bit_do_sterowania_1__1_oznacza_ze_jest_rowne[4]));
  or or_1 (przemiesc_kursor, komparator_7bit_do_sterowania_1__1_oznacza_ze_jest_rowne[0], komparator_7bit_do_sterowania_1__1_oznacza_ze_jest_rowne[1], komparator_7bit_do_sterowania_1__1_oznacza_ze_jest_rowne[2], komparator_7bit_do_sterowania_1__1_oznacza_ze_jest_rowne[3]);
  ROM #(.addrWidth(5), .dataWidth(3)) rom_1 (
    .addr(komparator_7bit_do_sterowania_1__1_oznacza_ze_jest_rowne), .data(_3_a_4_s_1_d_6_w_5_enter));  // open: sel

  // Notes on the sheet:
  //   contents of rom_1 (hex, n*v repeats v):
  //   0 3 4 0 1 0 0 0 6 7*0 5
endmodule

module uklad_zwracajacy_pozycje (
  input  [2:0] Sterowanie,
  input  Move,
  output [4:0] Poz_X,
  output [4:0] Poz_Y
);

  wire and_1_out, buffer_1_out, buffer_2_out, buffer_3_out, not_1_out;
  wire [2:0] counter_1_q, counter_2_q;

  not not_1 (not_1_out, Sterowanie[0]);
  buf buffer_1 (buffer_1_out, Sterowanie[1]);
  Counter #(.width(3), .max('h4), .trigger("falling")) counter_1 (
    .load(Sterowanie[1]), .D(counter_1_q), .count(Sterowanie[0]), .Q(counter_1_q), .clk(buffer_2_out));  // open: carry, clr
  buf buffer_2 (buffer_2_out, Move);
  Counter #(.width(3), .max('h4), .trigger("falling")) counter_2 (
    .load(buffer_1_out), .D(counter_2_q), .count(and_1_out), .Q(counter_2_q), .clk(buffer_3_out));  // open: carry, clr
  buf buffer_3 (buffer_3_out, Move);
  and and_1 (and_1_out, not_1_out, Sterowanie[2]);
  Shifter #(.width(5), .shift("rr")) shifter_1 (.in(5'b10000), .\dist (counter_1_q), .out(Poz_X));
  Shifter #(.width(5), .shift("rr")) shifter_2 (.in(5'b10000), .\dist (counter_2_q), .out(Poz_Y));

  // Other names for the same wires on the sheet: Control[2:0] = Sterowanie; M = Move
endmodule

module Uklad_zmiany_sterowania_z_3bit_na_5bit (
  input  [4:0] IN_X_5bit,
  input  [4:0] IN_Y_5bit,
  output [2:0] OUT_X__3bit,
  output [2:0] OUT_XY_3bit
);

  assign OUT_X__3bit = IN_X_5bit[0] ? 3'b100 : 3'bz;  // Controlled_Buffer controlled_buffer_1
  assign OUT_X__3bit = IN_X_5bit[1] ? 3'b011 : 3'bz;  // Controlled_Buffer controlled_buffer_2
  assign OUT_X__3bit = IN_X_5bit[4] ? 3'b000 : 3'bz;  // Controlled_Buffer controlled_buffer_3
  assign OUT_XY_3bit = IN_Y_5bit[0] ? 3'b100 : 3'bz;  // Controlled_Buffer controlled_buffer_4
  assign OUT_XY_3bit = IN_Y_5bit[1] ? 3'b011 : 3'bz;  // Controlled_Buffer controlled_buffer_5
  assign OUT_XY_3bit = IN_Y_5bit[4] ? 3'b000 : 3'bz;  // Controlled_Buffer controlled_buffer_6
  assign OUT_X__3bit = IN_X_5bit[2] ? 3'b010 : 3'bz;  // Controlled_Buffer controlled_buffer_7
  assign OUT_X__3bit = IN_X_5bit[3] ? 3'b001 : 3'bz;  // Controlled_Buffer controlled_buffer_8
  assign OUT_XY_3bit = IN_Y_5bit[2] ? 3'b010 : 3'bz;  // Controlled_Buffer controlled_buffer_9
  assign OUT_XY_3bit = IN_Y_5bit[3] ? 3'b001 : 3'bz;  // Controlled_Buffer controlled_buffer_10
endmodule

module Uklad_zwracania_pozycji_sasiednich_bitow (
  input  [4:0] Input_Y,
  input  [4:0] Input_X,
  output [2:0] out_3,
  output [5:0] LG,
  output [2:0] out_5,
  output [5:0] G,
  output [5:0] PG,
  output [5:0] P,
  output [5:0] DP,
  output [5:0] D,
  output [5:0] LD,
  output [5:0] L
);

  Uklad_zwracania_sasiednich_pomocniczy uklad_zwracania_sasiednich_pomocniczy_1 (
    .Input(Input_X), .Output_up(L[2:0]), .Output_down(DP[2:0]));
  Uklad_zwracania_sasiednich_pomocniczy uklad_zwracania_sasiednich_pomocniczy_2 (
    .Input(Input_Y), .Output_up(G[5:3]), .Output_down(D[5:3]));
  Uklad_zmiany_sterowania_z_3bit_na_5bit uklad_zmiany_sterowania_z_3bit_na_5bit_1 (
    .IN_X_5bit(Input_X), .IN_Y_5bit(Input_Y), .OUT_X__3bit(D[2:0]), .OUT_XY_3bit(L[5:3]));

  assign DP[5:3] = D[5:3];
  assign G[2:0] = D[2:0];
  assign LD = {D[5:3], L[2:0]};
  assign LG = {G[5:3], L[2:0]};
  assign out_3 = D[2:0];
  assign out_5 = L[5:3];
  assign P = {L[5:3], DP[2:0]};
  assign PG = {G[5:3], DP[2:0]};

  // Other names for the same wires on the sheet: INX[2:0] = D[2:0]; IN_X[4:0] = Input_X; IN_Y[4:0] = Input_Y;
  //   O_D_Y[2:0] = D[5:3]; O_L_X[2:0] = L[2:0]; O_P_X[2:0] = DP[2:0]; INY[2:0] = L[5:3]; O_U_Y[2:0] = G[5:3]
endmodule

module Uklad_zwracania_sasiednich_pomocniczy (
  input  [4:0] Input,
  output [2:0] Output_up,
  output [2:0] Output_down
);

  Multiplexer #(.select(5), .width(3)) multiplexer_1 (
    .in1(3'b011), .in2(3'b010), .in4(3'b001), .in8(3'b000), .in16(3'b000), .out(Output_up), .sel(Input));  // open: in0, in3, in5, in6, in7, in9, in10, in11, in12, in13, in14, in15, in17, in18, in19, in20, in21, in22, in23, in24, in25, in26, in27, in28, in29, in30, in31, en
  Multiplexer #(.select(5), .width(3)) multiplexer_2 (
    .in1(3'b100), .in2(3'b100), .in4(3'b011), .in8(3'b010), .in16(3'b001), .out(Output_down), .sel(Input));  // open: in0, in3, in5, in6, in7, in9, in10, in11, in12, in13, in14, in15, in17, in18, in19, in20, in21, in22, in23, in24, in25, in26, in27, in28, in29, in30, in31, en
endmodule

module Uklad_przesylu_wartosci_do_wyswietlania (
  input  [2:0] IN_Value,
  input  [2:0] IN_X,
  input  [2:0] IN_Y,
  output [2:0] O_00,
  output [2:0] O_01,
  output [2:0] O_02,
  output [2:0] O_03,
  output [2:0] O_04,
  output [2:0] O_05,
  output [2:0] O_06,
  output [2:0] O_07,
  output [2:0] O_08,
  output [2:0] O_09,
  output [2:0] O_10,
  output [2:0] O_11,
  output [2:0] O_12,
  output [2:0] O_13,
  output [2:0] O_14,
  output [2:0] O_15,
  output [2:0] O_16,
  output [2:0] O_17,
  output [2:0] O_18,
  output [2:0] O_19,
  output [2:0] O_20,
  output [2:0] O_21,
  output [2:0] O_22,
  output [2:0] O_23,
  output [2:0] O_24
);

  wire not_1_out;
  wire [4:0] controlled_buffer_1_out, Sterowanie_MUX;

  Multiplexer #(.select(3), .width(5)) multiplexer_1 (
    .in0(5'b00101), .in1(5'b00110), .in2(5'b00111), .in3(5'b11110), .in4({5{1'b1}}), .out(Sterowanie_MUX),
    .sel(IN_X));  // open: in5, in6, in7, en
  Demultiplexer #(.select(5), .width(3)) demultiplexer_1 (
    .out0(O_00), .out1(O_01), .out2(O_02), .out3(O_03), .out4(O_04), .out5(O_20), .out6(O_21), .out7(O_22),
    .out8(O_05), .out9(O_06), .out10(O_07), .out11(O_08), .out12(O_09), .out16(O_10), .out17(O_11),
    .out18(O_12), .out19(O_13), .out20(O_14), .out24(O_15), .out25(O_16), .out26(O_17), .out27(O_18),
    .out28(O_19), .out30(O_23), .out31(O_24), .in(IN_Value), .sel(controlled_buffer_1_out));  // open: out13, out14, out15, out21, out22, out23, out29, en
  assign controlled_buffer_1_out = not_1_out ? {IN_Y[1:0], IN_X} : 5'bz;  // Controlled_Buffer controlled_buffer_1
  not not_1 (not_1_out, IN_Y[2]);
  assign controlled_buffer_1_out = IN_Y[2] ? Sterowanie_MUX : 5'bz;  // Controlled_Buffer controlled_buffer_2

  // Other names for the same wires on the sheet: IN_V[2:0] = IN_Value; STER = IN_Y[2];
  //   Sterowanie_XY[4:0] = {IN_Y[1:0], IN_X}
endmodule
