// Logisim project Test nowego sterowania focusem.circ as structural Verilog: 1 circuit, main circuit main
module main (
  output [2:0] out_1,
  output [2:0] out_2,
  output [2:0] out_3,
  output [4:0] out_4
);

  wire clock_1_out, main_1_p3;
  wire [4:0] main_2_poz_x;
  wire [6:0] keyboard_1_data;

  Clock #(.highDuration(4), .lowDuration(2)) clock_1 (.out(clock_1_out));
  Keyboard #(.buflen(1)) keyboard_1 (.clk(clock_1_out), .data(keyboard_1_data));  // open: re, clr, avail
  // blok_sterowania2_main main_1: pin names not known; wires that end beside it: keyboard_1_data, out_3, main_1_p3
  blok_zwracajacy_pozycje_main main_2 (.Sterowanie(out_3), .Move(main_1_p3), .Poz_X(main_2_poz_x), .Poz_Y(out_4));
  \Układ_zmieny_sygnaly_sterowania_z_5bit_na_3bit_main  main_3 (
    .IN_X_5bit(main_2_poz_x), .IN_Y_5bit(out_4), .OUT_X__3bit(out_1), .OUT_XY_3bit(out_2));
  DotMatrix #(.inputtype("row"), .matrixrows(1)) dotmatrix_1 (.row0(main_2_poz_x));
  DotMatrix #(.matrixcols(1), .matrixrows(5)) dotmatrix_2 (.col0(out_4));
endmodule
