// Logisim project ukadz1.circ as structural Verilog: 1 circuit, main circuit main
module main (
  input  [4:0] in_1,
  output [27:0] out_2,
  output [20:0] out_3
);

  ROM #(.addrWidth(5), .dataWidth(28)) rom_1 (.addr(in_1), .data(out_2));  // open: sel
  ROM #(.addrWidth(5), .dataWidth(21)) rom_2 (.addr(in_1), .data(out_3));  // open: sel

  // Notes on the sheet:
  //   contents of rom_1 (hex, n*v repeats v):
  //   41 1020400 3810e00 3810e00 3850a00 3840e00 3840e00 810e00 3850e00 1020441 3810e41 3810e41 3850a41
  //   3840e41 3840e41 810e41 3850e41
  //   contents of rom_2 (hex, n*v repeats v):
  //   104000 408 e10 e04 204 e04 e14 204 e14 104408 104e10 104e04 104204 104e04 104e14 104204 104e14
endmodule
