// Logisim project uklad wysweitlania 1 koluny pol.circ as structural Verilog: 1 circuit, main circuit main
module main (
  input  [3:0] in_1,
  input  in_2
);

  wire [4:0] P1_2, P1_3, P1_4, P1_5;
  wire [29:0] d1;

  sterowanie_matryca_5x5_main main_1 (
    .stan(in_1), .focus(in_2), .O1(d1[4:0]), .O2(P1_2), .O3(P1_3), .O4(P1_4), .O5(P1_5));
  sterowanie_matryca_5x5_main main_2 (
    .stan(in_1), .focus(in_2), .O1(d1[19:15]), .O2(P1_2), .O3(P1_3), .O4(P1_4), .O5(P1_5));
  sterowanie_matryca_5x5_main main_3 (
    .stan(in_1), .focus(in_2), .O1(d1[9:5]), .O2(P1_2), .O3(P1_3), .O4(P1_4), .O5(P1_5));
  sterowanie_matryca_5x5_main main_4 (
    .stan(in_1), .focus(in_2), .O1(d1[24:20]), .O2(P1_2), .O3(P1_3), .O4(P1_4), .O5(P1_5));
  sterowanie_matryca_5x5_main main_5 (
    .stan(in_1), .focus(in_2), .O1(d1[14:10]), .O2(P1_2), .O3(P1_3), .O4(P1_4), .O5(P1_5));
  sterowanie_matryca_5x5_main main_6 (
    .stan(in_1), .focus(in_2), .O1(d1[29:25]), .O2(P1_2), .O3(P1_3), .O4(P1_4), .O5(P1_5));
  DotMatrix #(.matrixrows(30)) dotmatrix_1 (.col0(d1), .col1(d1), .col2(d1), .col3(d1), .col4(d1));

  // Other names for the same wires on the sheet: P1_1[4:0] = d1[4:0]; P2_1[4:0] = d1[9:5]; P3_1[4:0] = d1[14:10];
  //   P4_1[4:0] = d1[19:15]; P5_1[4:0] = d1[24:20]; P6_1[4:0] = d1[29:25]; f_1 = in_2; S_1[3:0] = in_1
endmodule
